// Logisim project computer.circ as structural Verilog: 1 circuit, main circuit main
module main (
  input  RESET
);

  wire and_1_out, clock_1_out, not_1_out, not_2_out, not_3_out;
  wire [2:0] counter_1_q;
  wire [6:0] controlled_buffer_5_out;
  wire [7:0] adder_1_out, controlled_buffer_1_out, controlled_buffer_2_out, controlled_buffer_3_out,
       controlled_buffer_4_out, controlled_buffer_9_out, controlled_buffer_10_out, controlled_buffer_11_out,
       controlled_buffer_13_out, counter_2_q, ram_1_data, register_1_q, register_2_q, register_3_q,
       register_4_q, register_5_q, subtractor_1_out;
  wire [11:0] rom_2_data;
  wire [13:11] adder_1_cout;
  wire [23:0] rom_1_data;

  Clock clock_1 (.out(clock_1_out));
  assign controlled_buffer_1_out = rom_1_data[11] ? {adder_1_cout[13], controlled_buffer_5_out} : 8'bz;  // Controlled_Buffer controlled_buffer_1
  Register register_1 (.D(controlled_buffer_3_out), .en(1'b1), .Q(register_1_q), .clk(and_1_out));  // open: clr
  Counter #(.width(3), .max('h7)) counter_1 (
    .Q(counter_1_q), .clk(not_1_out), .clr(RESET));  // open: load, D, count, carry
  not not_1 (not_1_out, and_1_out);
  assign controlled_buffer_2_out = rom_1_data[0] ? {adder_1_cout[13], controlled_buffer_5_out} : 8'bz;  // Controlled_Buffer controlled_buffer_2
  not not_2 (not_2_out, rom_1_data[1]);
  Register register_2 (.D(controlled_buffer_4_out), .Q(register_2_q), .clk(and_1_out), .clr(RESET));  // open: en
  RAM #(.bus("separate")) ram_1 (
    .addr(register_2_q), .din(controlled_buffer_1_out), .data(ram_1_data), .str(rom_1_data[11]), .sel(1'b1),
    .clk(and_1_out), .ld(rom_1_data[10]));  // open: clr
  assign controlled_buffer_3_out = rom_1_data[12] ? {adder_1_cout[13], controlled_buffer_5_out} : 8'bz;  // Controlled_Buffer controlled_buffer_3
  Register register_3 (.D(controlled_buffer_2_out), .en(1'b1), .Q(register_3_q), .clk(and_1_out), .clr(RESET));
  and and_1 (and_1_out, not_2_out, clock_1_out);
  assign controlled_buffer_4_out = rom_1_data[9] ? {adder_1_cout[13], controlled_buffer_5_out} : 8'bz;  // Controlled_Buffer controlled_buffer_4
  assign {adder_1_cout[13], controlled_buffer_5_out} = rom_1_data[10] ? ram_1_data : 8'bz;  // Controlled_Buffer controlled_buffer_5
  ROM #(.addrWidth(16), .dataWidth(24)) rom_1 (
    .addr({2'b00, adder_1_cout, register_1_q, counter_1_q}), .data(rom_1_data), .sel(1'b1));
  assign {adder_1_cout[13], controlled_buffer_5_out} = rom_1_data[13] ? register_4_q : 8'bz;  // Controlled_Buffer controlled_buffer_6
  assign {adder_1_cout[13], controlled_buffer_5_out} = rom_1_data[7] ? controlled_buffer_11_out : 8'bz;  // Controlled_Buffer controlled_buffer_7
  Hex_Digit_Display hex_digit_display_1 (.value(rom_2_data[11:8]));  // open: dp
  ROM #(.dataWidth(12)) rom_2 (.addr(register_3_q), .data(rom_2_data));  // open: sel
  assign {adder_1_cout[13], controlled_buffer_5_out} = rom_1_data[2] ? counter_2_q : 8'bz;  // Controlled_Buffer controlled_buffer_8
  assign controlled_buffer_9_out = rom_1_data[3] ? {adder_1_cout[13], controlled_buffer_5_out} : 8'bz;  // Controlled_Buffer controlled_buffer_9
  assign controlled_buffer_10_out = rom_1_data[6] ? {adder_1_cout[13], controlled_buffer_5_out} : 8'bz;  // Controlled_Buffer controlled_buffer_10
  nand nand_1 (adder_1_cout[12], controlled_buffer_5_out[0], controlled_buffer_5_out[1], controlled_buffer_5_out[2], controlled_buffer_5_out[3], controlled_buffer_5_out[4], controlled_buffer_5_out[5], controlled_buffer_5_out[6], adder_1_cout[13]);
  Hex_Digit_Display hex_digit_display_2 (.value(rom_2_data[7:4]));  // open: dp
  Counter counter_2 (
    .load(rom_1_data[3]), .D(controlled_buffer_9_out), .count(rom_1_data[4]), .Q(counter_2_q),
    .clk(and_1_out), .clr(RESET));  // open: carry
  Register register_4 (.D(controlled_buffer_10_out), .en(1'b1), .Q(register_4_q), .clk(and_1_out));  // open: clr
  assign controlled_buffer_11_out = not_3_out ? adder_1_out : 8'bz;  // Controlled_Buffer controlled_buffer_11
  Adder adder_1 (.a(register_4_q), .b(register_5_q), .out(adder_1_out), .cout(adder_1_cout[11]));  // open: cin
  Hex_Digit_Display hex_digit_display_3 (.value(rom_2_data[3:0]));  // open: dp
  Subtractor subtractor_1 (.a(register_4_q), .b(register_5_q), .out(subtractor_1_out));  // open: bin, bout
  not not_3 (not_3_out, rom_1_data[8]);
  assign controlled_buffer_11_out = rom_1_data[8] ? subtractor_1_out : 8'bz;  // Controlled_Buffer controlled_buffer_12
  assign controlled_buffer_13_out = rom_1_data[5] ? {adder_1_cout[13], controlled_buffer_5_out} : 8'bz;  // Controlled_Buffer controlled_buffer_13
  Register register_5 (.D(controlled_buffer_13_out), .en(1'b1), .Q(register_5_q), .clk(and_1_out));  // open: clr

  // Notes on the sheet:
  //   RAM
  //   Memory Register
  //   Input Register
  //   Clock
  //   contents of rom_1 (hex, n*v repeats v):
  //   204 1410 6*0 204 1410 204 430 c0 0 0 0 204 1410 204 610 420 c0 0 0 204 1410 204 408 4*0 204 1410
  //   2001 5*0 204 1410 204 610 2800 0 0 0 204 1410 204 450 4*0 204 1410 6*0 204 1410 6*0 204 1410 6*0 204
  //   1410 6*0 204 1410 6*0 204 1410 6*0 204 1410 6*0 204 1410 6*0 204 1410 6*0 204 1410 6*0 204 1410 6*0
  //   204 1410 6*0 204 1410 6*0 204 1410 6*0 204 1410 6*0 204 1410 6*0 204 1410 6*0 204 1410 6*0 204 1410
  //   6*0 204 1410 6*0 204 1410 6*0 204 1410 6*0 204 1410 6*0 204 1410 6*0 204 1410 6*0 204 1410 6*0 204
  //   1410 6*0 204 1410 6*0 204 1410 6*0 204 1410 6*0 204 1410 6*0 204 1410 6*0 204 1410 6*0 204 1410 6*0
  //   204 1410 6*0 204 1410 6*0 204 1410 6*0 204 1410 6*0 204 1410 6*0 204 1410 6*0 204 1410 6*0 204 1410
  //   6*0 204 1410 6*0 204 1410 6*0 204 1410 6*0 204 1410 6*0 204 1410 6*0 204 1410 6*0 204 1410 6*0 204
  //   1410 6*0 204 1410 6*0 204 1410 6*0 204 1410 6*0 204 1410 6*0 204 1410 6*0 204 1410 6*0 204 1410 6*0
  //   204 1410 6*0 204 1410 6*0 204 1410 6*0 204 1410 6*0 204 1410 6*0 204 1410 6*0 204 1410 6*0 204 1410
  //   6*0 204 1410 6*0 204 1410 6*0 204 1410 6*0 204 1410 6*0 204 1410 6*0 204 1410 6*0 204 1410 6*0 204
  //   1410 6*0 204 1410 6*0 204 1410 6*0 204 1410 6*0 204 1410 6*0 204 1410 6*0 204 1410 6*0 204 1410 6*0
  //   204 1410 6*0 204 1410 6*0 204 1410 6*0 204 1410 6*0 204 1410 6*0 204 1410 6*0 204 1410 6*0 204 1410
  //   6*0 204 1410 6*0 204 1410 6*0 204 1410 6*0 204 1410 6*0 204 1410 6*0 204 1410 6*0 204 1410 6*0 204
  //   1410 6*0 204 1410 6*0 204 1410 6*0 204 1410 6*0 204 1410 6*0 204 1410 6*0 204 1410 6*0 204 1410 6*0
  //   204 1410 6*0 204 1410 6*0 204 1410 6*0 204 1410 6*0 204 1410 6*0 204 1410 6*0 204 1410 6*0 204 1410
  //   6*0 204 1410 6*0 204 1410 6*0 204 1410 6*0 204 1410 6*0 204 1410 6*0 204 1410 6*0 204 1410 6*0 204
  //   1410 6*0 204 1410 6*0 204 1410 6*0 204 1410 6*0 204 1410 6*0 204 1410 6*0 204 1410 6*0 204 1410 6*0
  //   204 1410 6*0 204 1410 6*0 204 1410 6*0 204 1410 6*0 204 1410 6*0 204 1410 6*0 204 1410 6*0 204 1410
  //   6*0 204 1410 6*0 204 1410 6*0 204 1410 6*0 204 1410 6*0 204 1410 6*0 204 1410 6*0 204 1410 6*0 204
  //   1410 6*0 204 1410 6*0 204 1410 6*0 204 1410 6*0 204 1410 6*0 204 1410 6*0 204 1410 6*0 204 1410 6*0
  //   204 1410 6*0 204 1410 6*0 204 1410 6*0 204 1410 6*0 204 1410 6*0 204 1410 6*0 204 1410 6*0 204 1410
  //   6*0 204 1410 6*0 204 1410 6*0 204 1410 6*0 204 1410 6*0 204 1410 6*0 204 1410 6*0 204 1410 6*0 204
  //   1410 6*0 204 1410 6*0 204 1410 6*0 204 1410 6*0 204 1410 6*0 204 1410 6*0 204 1410 6*0 204 1410 6*0
  //   204 1410 6*0 204 1410 6*0 204 1410 6*0 204 1410 6*0 204 1410 6*0 204 1410 6*0 204 1410 6*0 204 1410
  //   6*0 204 1410 6*0 204 1410 6*0 204 1410 6*0 204 1410 6*0 204 1410 6*0 204 1410 6*0 204 1410 6*0 204
  //   1410 6*0 204 1410 6*0 204 1410 6*0 204 1410 6*0 204 1410 6*0 204 1410 6*0 204 1410 6*0 204 1410 6*0
  //   204 1410 6*0 204 1410 6*0 204 1410 6*0 204 1410 6*0 204 1410 6*0 204 1410 6*0 204 1410 6*0 204 1410
  //   6*0 204 1410 6*0 204 1410 6*0 204 1410 6*0 204 1410 6*0 204 1410 6*0 204 1410 6*0 204 1410 6*0 204
  //   1410 6*0 204 1410 6*0 204 1410 6*0 204 1410 6*0 204 1410 6*0 204 1410 6*0 204 1410 6*0 204 1410 6*0
  //   204 1410 6*0 204 1410 6*0 204 1410 6*0 204 1410 6*0 204 1410 6*0 204 1410 6*0 204 1410 6*0 204 1410
  //   6*0 204 1410 6*0 204 1410 6*0 204 1410 6*0 204 1410 6*0 204 1410 6*0 204 1410 6*0 204 1410 6*0 204
  //   1410 6*0 204 1410 6*0 204 1410 6*0 204 1410 6*0 204 1410 6*0 204 1410 6*0 204 1410 6*0 204 1410 6*0
  //   204 1410 6*0 204 1410 6*0 204 1410 6*0 204 1410 6*0 204 1410 6*0 204 1410 6*0 204 1410 6*0 204 1410
  //   2 5*0 204 1410 6*0 204 1410 204 430 c0 0 0 0 204 1410 204 610 420 c0 0 0 204 1410 204 408 4*0 204
  //   1410 2001 5*0 204 1410 204 610 2800 0 0 0 204 1410 204 450 4*0 204 1410 6*0 204 1410 6*0 204 1410
  //   6*0 204 1410 6*0 204 1410 6*0 204 1410 6*0 204 1410 6*0 204 1410 6*0 204 1410 6*0 204 1410 6*0 204
  //   1410 6*0 204 1410 6*0 204 1410 6*0 204 1410 6*0 204 1410 6*0 204 1410 6*0 204 1410 6*0 204 1410 6*0
  //   204 1410 6*0 204 1410 6*0 204 1410 6*0 204 1410 6*0 204 1410 6*0 204 1410 6*0 204 1410 6*0 204 1410
  //   6*0 204 1410 6*0 204 1410 6*0 204 1410 6*0 204 1410 6*0 204 1410 6*0 204 1410 6*0 204 1410 6*0 204
  //   1410 6*0 204 1410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
  //   contents of rom_2 (hex, n*v repeats v):
  //   0 1 2 3 4 5 6 7 8 9 10 11 12 13 14 15 16 17 18 19 20 21 22 23 24 25 26 27 28 29 30 31 32 33 34 35 36
  //   37 38 39 40 41 42 43 44 45 46 47 48 49 50 51 52 53 54 55 56 57 58 59 60 61 62 63 64 65 66 67 68 69
  //   70 71 72 73 74 75 76 77 78 79 80 81 82 83 84 85 86 87 88 89 90 91 92 93 94 95 96 97 98 99 100 101
  //   102 103 104 105 106 107 108 109 110 111 112 113 114 115 116 117 118 119 120 121 122 123 124 125 126
  //   127 128 129 130 131 132 133 134 135 136 137 138 139 140 141 142 143 144 145 146 147 148 149 150 151
  //   152 153 154 155 156 157 158 159 160 161 162 163 164 165 166 167 168 169 170 171 172 173 174 175 176
  //   177 178 179 180 181 182 183 184 185 186 187 188 189 190 191 192 193 194 195 196 197 198 199 200 201
  //   202 203 204 205 206 207 208 209 210 211 212 213 214 215 216 217 218 219 220 221 222 223 224 225 226
  //   227 228 229 230 231 232 233 234 235 236 237 238 239 240 241 242 243 244 245 246 247 248 249 250 251
  //   252 253 254 255
  //   Program Counter
  //   Adder
  //   CF
  //   ZF
  //   SF
  //   A Register
  //   AO
  //   MI
  //   II
  //   MO
  //   MA
  //   SUB
  //   B register
  //   BI
  //   CE
  //   CI
  //   AI
  //   EO
  //   CO
  //   DI
  //   HLT
endmodule
